// Digital circuit ALU.dig as structural Verilog
module ALU (
  input  [7:0] ACin,
  input  [7:0] N,
  input  CLK,
  input  [2:0] Sel,
  output [7:0] AC,
  output [7:0] MQ
);

  wire [7:0] divisor_bits_1_resto, logical_shift_1_acout, logical_shift_2_acout, MQ0, MQ1, multiplexer_1_out,
       multiplexer_2_out, multiplicador_8bits_1_ac, nand_1_out, somador_8bits_1_s, subtrator_8bits_1_s,
       xor_1_out;

  somador_8bits somador_8bits_1 (.Ci(1'b0), .A(ACin), .B(N), .S(somador_8bits_1_s));  // open: Cout
  subtrator_8bits subtrator_8bits_1 (.A(ACin), .B(N), .S(subtrator_8bits_1_s));  // open: Cout
  multiplicador_8bits multiplicador_8bits_1 (.A(ACin), .B(N), .MQ(MQ0), .AC(multiplicador_8bits_1_ac));
  divisor_bits divisor_bits_1 (.AC(ACin), .N(N), .Resto(divisor_bits_1_resto), .MQ(MQ1));
  logical_shift logical_shift_1 (.ACin(ACin), .Direita(1'b0), .ACout(logical_shift_1_acout));
  logical_shift logical_shift_2 (.ACin(ACin), .Direita(1'b1), .ACout(logical_shift_2_acout));
  assign nand_1_out = ~(ACin & N);  // NAnd nand_1, 8 bits wide
  assign xor_1_out = ACin ^ N;  // XOr xor_1, 8 bits wide
  Multiplexer #(.Bits(8), .Selector_Bits(3)) multiplexer_1 (
    .sel(Sel), .in_0(somador_8bits_1_s), .in_1(subtrator_8bits_1_s), .in_2(multiplicador_8bits_1_ac),
    .in_3(divisor_bits_1_resto), .in_4(logical_shift_1_acout), .in_5(logical_shift_2_acout),
    .in_6(nand_1_out), .in_7(xor_1_out), .out(multiplexer_1_out));
  Multiplexer #(.Selector_Bits(3), .Bits(8)) multiplexer_2 (
    .sel(Sel), .in_0({8{1'b0}}), .in_1({8{1'b0}}), .in_2(MQ0), .in_3(MQ1), .in_4({8{1'b0}}),
    .in_5({8{1'b0}}), .in_6({8{1'b0}}), .in_7({8{1'b0}}), .out(multiplexer_2_out));
  Register #(.Bits(8)) register_1 (.D(multiplexer_1_out), .C(CLK), .en(1'b1), .Q(AC));
  Register #(.Bits(8)) register_2 (.D(multiplexer_2_out), .C(CLK), .en(1'b1), .Q(MQ));
  Seven_Seg_Hex seven_seg_hex_1 (.d(AC[7:4]), .dp(1'b0));
  Seven_Seg_Hex seven_seg_hex_2 (.d(AC[3:0]), .dp(1'b0));
  Seven_Seg_Hex seven_seg_hex_3 (.d(MQ[7:4]), .dp(1'b0));
  Seven_Seg_Hex seven_seg_hex_4 (.d(MQ[3:0]), .dp(1'b0));

  // Notes on the sheet:
  //   AC
  //   MQ
endmodule
