// Digital circuit divisor_8bits.dig as structural Verilog
module divisor_8bits (
  input  A,
  input  [7:0] Pi,
  input  [7:0] N,
  output [7:0] Po,
  output Qi
);

  wire [7:0] S;

  Multiplexer #(.Bits(8)) multiplexer_1 (.sel(S[7]), .in_0(S), .in_1({Pi[6:0], A}), .out(Po));
  subtrator_8bits subtrator_8bits_1 (.A({Pi[6:0], A}), .B(N), .S(S));  // open: Cout
  not not_1 (Qi, S[7]);

  // Other names for the same wires on the sheet: PS[7:0] = {Pi[6:0], A}; P0 = Pi[0]; P1 = Pi[1]; P2 = Pi[2];
  //   P3 = Pi[3]; P4 = Pi[4]; P5 = Pi[5]; P6 = Pi[6]; P7 = Pi[7]; S0[6:0] = S[6:0]; S1 = S[7]
endmodule
