// Digital circuit divisor_bits.dig as structural Verilog
module divisor_bits (
  input  [7:0] AC,
  input  [7:0] N,
  output [7:0] Resto,
  output [7:0] MQ
);

  wire [7:0] divisor_8bits_1_po, divisor_8bits_2_po, divisor_8bits_3_po, divisor_8bits_4_po,
       divisor_8bits_5_po, divisor_8bits_6_po, divisor_8bits_7_po;

  divisor_8bits divisor_8bits_1 (.A(AC[7]), .Pi({8{1'b0}}), .N(N), .Po(divisor_8bits_1_po), .Qi(MQ[7]));
  divisor_8bits divisor_8bits_2 (.A(AC[6]), .Pi(divisor_8bits_1_po), .N(N), .Po(divisor_8bits_2_po), .Qi(MQ[6]));
  divisor_8bits divisor_8bits_3 (.A(AC[5]), .Pi(divisor_8bits_2_po), .N(N), .Po(divisor_8bits_3_po), .Qi(MQ[5]));
  divisor_8bits divisor_8bits_4 (.A(AC[4]), .Pi(divisor_8bits_3_po), .N(N), .Po(divisor_8bits_4_po), .Qi(MQ[4]));
  divisor_8bits divisor_8bits_5 (.A(AC[3]), .Pi(divisor_8bits_4_po), .N(N), .Po(divisor_8bits_5_po), .Qi(MQ[3]));
  divisor_8bits divisor_8bits_6 (.A(AC[2]), .Pi(divisor_8bits_5_po), .N(N), .Po(divisor_8bits_6_po), .Qi(MQ[2]));
  divisor_8bits divisor_8bits_7 (.A(AC[1]), .Pi(divisor_8bits_6_po), .N(N), .Po(divisor_8bits_7_po), .Qi(MQ[1]));
  divisor_8bits divisor_8bits_8 (.A(AC[0]), .Pi(divisor_8bits_7_po), .N(N), .Po(Resto), .Qi(MQ[0]));

  // Other names for the same wires on the sheet: Q0 = MQ[0]; Q1 = MQ[1]; Q2 = MQ[2]; Q3 = MQ[3]; Q4 = MQ[4];
  //   Q5 = MQ[5]; Q6 = MQ[6]; Q7 = MQ[7]
endmodule
