// Digital circuit logical_shift.dig as structural Verilog
module logical_shift (
  input  [7:0] ACin,
  input  Direita,
  output [7:0] ACout
);

  Multiplexer #(.Bits(8)) multiplexer_1 (
    .sel(Direita), .in_0({ACin[6:0], 1'b0}), .in_1({1'b0, ACin[7:1]}), .out(ACout));

  // Other names for the same wires on the sheet: AC0 = ACin[0]; AC1 = ACin[1]; AC2 = ACin[2]; AC3 = ACin[3];
  //   AC4 = ACin[4]; AC5 = ACin[5]; AC6 = ACin[6]; AC7 = ACin[7]
endmodule
