// Digital circuit multiplicador_8bits.dig as structural Verilog
module multiplicador_8bits (
  input  [7:0] A,
  input  [7:0] B,
  output [7:0] MQ,
  output [7:0] AC
);

  wire [6:0] and_8_out;
  wire [7:0] and_16_out, and_24_out, and_32_out, and_40_out, and_48_out, and_56_out, and_64_out,
       somador_8bits_1_cout, somador_8bits_2_cout, somador_8bits_3_cout, somador_8bits_4_cout,
       somador_8bits_5_cout, somador_8bits_6_cout;

  and and_1 (AC[0], A[0], B[0]);
  and and_2 (and_8_out[0], A[1], B[0]);
  and and_3 (and_8_out[1], A[2], B[0]);
  and and_4 (and_8_out[2], A[3], B[0]);
  and and_5 (and_8_out[3], A[4], B[0]);
  and and_6 (and_8_out[4], A[5], B[0]);
  and and_7 (and_8_out[5], A[6], B[0]);
  and and_8 (and_8_out[6], A[7], B[0]);
  and and_9 (and_16_out[0], A[0], B[1]);
  and and_10 (and_16_out[1], A[1], B[1]);
  and and_11 (and_16_out[2], A[2], B[1]);
  and and_12 (and_16_out[3], A[3], B[1]);
  and and_13 (and_16_out[4], A[4], B[1]);
  and and_14 (and_16_out[5], A[5], B[1]);
  and and_15 (and_16_out[6], A[6], B[1]);
  and and_16 (and_16_out[7], A[7], B[1]);
  somador_8bits somador_8bits_1 (
    .Ci(1'b0), .A({1'b0, and_8_out}), .B(and_16_out), .S({somador_8bits_1_cout[6:0], AC[1]}),
    .Cout(somador_8bits_1_cout[7]));
  and and_17 (and_24_out[0], A[0], B[2]);
  and and_18 (and_24_out[1], A[1], B[2]);
  and and_19 (and_24_out[2], A[2], B[2]);
  and and_20 (and_24_out[3], A[3], B[2]);
  and and_21 (and_24_out[4], A[4], B[2]);
  and and_22 (and_24_out[5], A[5], B[2]);
  and and_23 (and_24_out[6], A[6], B[2]);
  and and_24 (and_24_out[7], A[7], B[2]);
  somador_8bits somador_8bits_2 (
    .Ci(1'b0), .A(somador_8bits_1_cout), .B(and_24_out), .S({somador_8bits_2_cout[6:0], AC[2]}),
    .Cout(somador_8bits_2_cout[7]));
  and and_25 (and_32_out[0], A[0], B[3]);
  and and_26 (and_32_out[1], A[1], B[3]);
  and and_27 (and_32_out[2], A[2], B[3]);
  and and_28 (and_32_out[3], A[3], B[3]);
  and and_29 (and_32_out[4], A[4], B[3]);
  and and_30 (and_32_out[5], A[5], B[3]);
  and and_31 (and_32_out[6], A[6], B[3]);
  and and_32 (and_32_out[7], A[7], B[3]);
  somador_8bits somador_8bits_3 (
    .Ci(1'b0), .A(somador_8bits_2_cout), .B(and_32_out), .S({somador_8bits_3_cout[6:0], AC[3]}),
    .Cout(somador_8bits_3_cout[7]));
  and and_33 (and_40_out[0], A[0], B[4]);
  and and_34 (and_40_out[1], A[1], B[4]);
  and and_35 (and_40_out[2], A[2], B[4]);
  and and_36 (and_40_out[3], A[3], B[4]);
  and and_37 (and_40_out[4], A[4], B[4]);
  and and_38 (and_40_out[5], A[5], B[4]);
  and and_39 (and_40_out[6], A[6], B[4]);
  and and_40 (and_40_out[7], A[7], B[4]);
  somador_8bits somador_8bits_4 (
    .Ci(1'b0), .A(somador_8bits_3_cout), .B(and_40_out), .S({somador_8bits_4_cout[6:0], AC[4]}),
    .Cout(somador_8bits_4_cout[7]));
  and and_41 (and_48_out[0], A[0], B[5]);
  and and_42 (and_48_out[1], A[1], B[5]);
  and and_43 (and_48_out[2], A[2], B[5]);
  and and_44 (and_48_out[3], A[3], B[5]);
  and and_45 (and_48_out[4], A[4], B[5]);
  and and_46 (and_48_out[5], A[5], B[5]);
  and and_47 (and_48_out[6], A[6], B[5]);
  and and_48 (and_48_out[7], A[7], B[5]);
  somador_8bits somador_8bits_5 (
    .Ci(1'b0), .A(somador_8bits_4_cout), .B(and_48_out), .S({somador_8bits_5_cout[6:0], AC[5]}),
    .Cout(somador_8bits_5_cout[7]));
  and and_49 (and_56_out[0], A[0], B[6]);
  and and_50 (and_56_out[1], A[1], B[6]);
  and and_51 (and_56_out[2], A[2], B[6]);
  and and_52 (and_56_out[3], A[3], B[6]);
  and and_53 (and_56_out[4], A[4], B[6]);
  and and_54 (and_56_out[5], A[5], B[6]);
  and and_55 (and_56_out[6], A[6], B[6]);
  and and_56 (and_56_out[7], A[7], B[6]);
  somador_8bits somador_8bits_6 (
    .Ci(1'b0), .A(somador_8bits_5_cout), .B(and_56_out), .S({somador_8bits_6_cout[6:0], AC[6]}),
    .Cout(somador_8bits_6_cout[7]));
  and and_57 (and_64_out[0], A[0], B[7]);
  and and_58 (and_64_out[1], A[1], B[7]);
  and and_59 (and_64_out[2], A[2], B[7]);
  and and_60 (and_64_out[3], A[3], B[7]);
  and and_61 (and_64_out[4], A[4], B[7]);
  and and_62 (and_64_out[5], A[5], B[7]);
  and and_63 (and_64_out[6], A[6], B[7]);
  and and_64 (and_64_out[7], A[7], B[7]);
  somador_8bits somador_8bits_7 (
    .Ci(1'b0), .A(somador_8bits_6_cout), .B(and_64_out), .S({MQ[6:0], AC[7]}), .Cout(MQ[7]));

  // Other names for the same wires on the sheet: S7 = AC[7]; S8 = MQ[0]; S9 = MQ[1]; S10 = MQ[2]; S11 = MQ[3];
  //   S12 = MQ[4]; S13 = MQ[5]; S14 = MQ[6]; S6 = AC[6]; S5 = AC[5]; S4 = AC[4]; S3 = AC[3]; S2 = AC[2]; S1 = AC[1];
  //   S0 = AC[0]; S15 = MQ[7]
endmodule
