// Digital circuit somador_4bits.dig as structural Verilog
module somador_4bits (
  input  Ci,
  input  [3:0] A,
  input  [3:0] B,
  output [3:0] S,
  output Co
);

  wire somador_1bits_1_cout, somador_1bits_2_cout, somador_1bits_3_cout;

  somador_1bits somador_1bits_1 (.Ci(Ci), .A(A[0]), .B(B[0]), .S(S[0]), .Cout(somador_1bits_1_cout));
  somador_1bits somador_1bits_2 (.Ci(somador_1bits_1_cout), .A(A[1]), .B(B[1]), .S(S[1]), .Cout(somador_1bits_2_cout));
  somador_1bits somador_1bits_3 (.Ci(somador_1bits_2_cout), .A(A[2]), .B(B[2]), .S(S[2]), .Cout(somador_1bits_3_cout));
  somador_1bits somador_1bits_4 (.Ci(somador_1bits_3_cout), .A(A[3]), .B(B[3]), .S(S[3]), .Cout(Co));
endmodule
