// Digital circuit somador_8bits.dig as structural Verilog
module somador_8bits (
  input  Ci,
  input  [7:0] A,
  input  [7:0] B,
  output [7:0] S,
  output Cout
);

  wire somador_1bits_1_cout, somador_1bits_2_cout, somador_1bits_3_cout, somador_1bits_4_cout,
       somador_1bits_5_cout, somador_1bits_6_cout, somador_1bits_7_cout;

  somador_1bits somador_1bits_1 (.Ci(Ci), .A(A[0]), .B(B[0]), .S(S[0]), .Cout(somador_1bits_1_cout));
  somador_1bits somador_1bits_2 (.Ci(somador_1bits_1_cout), .A(A[1]), .B(B[1]), .S(S[1]), .Cout(somador_1bits_2_cout));
  somador_1bits somador_1bits_3 (.Ci(somador_1bits_2_cout), .A(A[2]), .B(B[2]), .S(S[2]), .Cout(somador_1bits_3_cout));
  somador_1bits somador_1bits_4 (.Ci(somador_1bits_3_cout), .A(A[3]), .B(B[3]), .S(S[3]), .Cout(somador_1bits_4_cout));
  somador_1bits somador_1bits_5 (.Ci(somador_1bits_4_cout), .A(A[4]), .B(B[4]), .S(S[4]), .Cout(somador_1bits_5_cout));
  somador_1bits somador_1bits_6 (.Ci(somador_1bits_5_cout), .A(A[5]), .B(B[5]), .S(S[5]), .Cout(somador_1bits_6_cout));
  somador_1bits somador_1bits_7 (.Ci(somador_1bits_6_cout), .A(A[6]), .B(B[6]), .S(S[6]), .Cout(somador_1bits_7_cout));
  somador_1bits somador_1bits_8 (.Ci(somador_1bits_7_cout), .A(A[7]), .B(B[7]), .S(S[7]), .Cout(Cout));
endmodule
