// Digital circuit subtrator_8bits.dig as structural Verilog
module subtrator_8bits (
  input  [7:0] A,
  input  [7:0] B,
  output [7:0] S,
  output Cout
);

  wire not_1_out, not_2_out, not_3_out, not_4_out, not_5_out, not_6_out, not_7_out, not_8_out,
       somador_1bits_1_cout, somador_1bits_2_cout, somador_1bits_3_cout, somador_1bits_4_cout,
       somador_1bits_5_cout, somador_1bits_6_cout, somador_1bits_7_cout;

  somador_1bits somador_1bits_1 (.Ci(1'b1), .A(A[0]), .B(not_1_out), .S(S[0]), .Cout(somador_1bits_1_cout));
  not not_1 (not_1_out, B[0]);
  somador_1bits somador_1bits_2 (
    .Ci(somador_1bits_1_cout), .A(A[1]), .B(not_2_out), .S(S[1]), .Cout(somador_1bits_2_cout));
  not not_2 (not_2_out, B[1]);
  somador_1bits somador_1bits_3 (
    .Ci(somador_1bits_2_cout), .A(A[2]), .B(not_3_out), .S(S[2]), .Cout(somador_1bits_3_cout));
  not not_3 (not_3_out, B[2]);
  somador_1bits somador_1bits_4 (
    .Ci(somador_1bits_3_cout), .A(A[3]), .B(not_4_out), .S(S[3]), .Cout(somador_1bits_4_cout));
  not not_4 (not_4_out, B[3]);
  somador_1bits somador_1bits_5 (
    .Ci(somador_1bits_4_cout), .A(A[4]), .B(not_5_out), .S(S[4]), .Cout(somador_1bits_5_cout));
  not not_5 (not_5_out, B[4]);
  somador_1bits somador_1bits_6 (
    .Ci(somador_1bits_5_cout), .A(A[5]), .B(not_6_out), .S(S[5]), .Cout(somador_1bits_6_cout));
  not not_6 (not_6_out, B[5]);
  somador_1bits somador_1bits_7 (
    .Ci(somador_1bits_6_cout), .A(A[6]), .B(not_7_out), .S(S[6]), .Cout(somador_1bits_7_cout));
  not not_7 (not_7_out, B[6]);
  somador_1bits somador_1bits_8 (.Ci(somador_1bits_7_cout), .A(A[7]), .B(not_8_out), .S(S[7]), .Cout(Cout));
  not not_8 (not_8_out, B[7]);
  LED plus (.in(S[7]));
endmodule
